// Digital circuit MMYY.dig as structural Verilog
module MMYY (
  input  [15:0] A,
  input  [15:0] B,
  output [15:0] out_3
);

  wire [15:0] decoder32_16_16_1_a, decoder32_16_16_1_b;

  decoder32_16_16 decoder32_16_16_1 (.Ip({B, A}), .A(decoder32_16_16_1_a), .B(decoder32_16_16_1_b));
  addingThing addingthing_1 (.a(decoder32_16_16_1_a), .b(decoder32_16_16_1_b), .op(out_3));
endmodule
