// Digital circuit addingThing.dig as structural Verilog
module addingThing (
  input  [15:0] a,
  input  [15:0] b,
  output [15:0] op
);

  Add #(.Bits(16)) add_1 (.a(a), .b(b), .c_i(1'b0), .s(op));  // open: c_o
endmodule
