// Digital circuit decoder32,16,16.dig as structural Verilog
module decoder32_16_16 (
  input  [31:0] Ip,
  output [15:0] A,
  output [15:0] B
);


  assign A = Ip[15:0];
  assign B = Ip[31:16];
endmodule
